// Logisim project circuito_vetorial.circ as structural Verilog: 6 circuits, main circuit main
module main (
);

  wire adder_1_cout;
  wire [3:0] Opcode, Resto;
  wire [7:0] register_1_q, undriven;

  Adder adder_1 (.a(register_1_q), .b(undriven), .cin(1'b0), .cout(adder_1_cout));  // open: out
  LED led_1 (.in(adder_1_cout));
  Register register_1 (.Q(register_1_q));  // open: D, en, clk, clr
  ROM MemInstrucao (.addr(register_1_q), .data({Opcode, Resto}));
  Decodificador decodificador_1 (.A(Opcode));  // open: B
  BR_vet br_vet_1 ();  // open: Reset, Clk, Dados, R0, WriteReg, RW, RA, RB, A, B
  BR_vet br_vet_2 ();  // open: Reset, Clk, Dados, R0, WriteReg, RW, RA, RB, A, B
  BR_vet br_vet_3 ();  // open: Reset, Clk, Dados, R0, WriteReg, RW, RA, RB, A, B
  BR_vet br_vet_4 ();  // open: Reset, Clk, Dados, R0, WriteReg, RW, RA, RB, A, B
  BR_seq br_seq_1 ();  // open: Reset, Clk, Dados, WriteReg, RW, RA, RB, A, B
  ULA_vet ula_vet_1 ();  // open: A, B, Funct, S
  ULA_vet ula_vet_2 ();  // open: A, B, Funct, S
  ULA_vet ula_vet_3 ();  // open: A, B, Funct, S
  ULA_vet ula_vet_4 ();  // open: A, B, Funct, S
  ULA_seq ula_seq_1 ();  // open: A, B, Funct, S
  ROM rom_1 ();  // open: addr, data
  ROM MemDadosVet_1 ();  // open: addr, data
  ROM MemDadosVet_2 ();  // open: addr, data
  ROM MemDadosVet_3 ();  // open: addr, data
  ROM MemDadosVet_4 ();  // open: addr, data
endmodule

module BR_seq (
  input  Reset,
  input  Clk,
  input  [7:0] Dados,
  input  WriteReg,
  input  [1:0] RW,
  input  [1:0] RA,
  input  [1:0] RB,
  output [7:0] A,
  output [7:0] B
);

  wire demultiplexer_1_out0, demultiplexer_1_out1, demultiplexer_1_out2, demultiplexer_1_out3;
  wire [7:0] R0_q, R1_q, R2_q, R3_q;

  Demultiplexer #(.select(2)) demultiplexer_1 (
    .out0(demultiplexer_1_out0), .out1(demultiplexer_1_out1), .out2(demultiplexer_1_out2),
    .out3(demultiplexer_1_out3), .in(WriteReg), .sel(RW));
  Register R0 (.D({8{1'b0}}), .en(demultiplexer_1_out0), .clk(Clk), .Q(R0_q), .clr(Reset));
  Register R1 (.D(Dados), .en(demultiplexer_1_out1), .clk(Clk), .Q(R1_q), .clr(Reset));
  Register R2 (.D(Dados), .en(demultiplexer_1_out2), .clk(Clk), .Q(R2_q), .clr(Reset));
  Register R3 (.D(Dados), .en(demultiplexer_1_out3), .clk(Clk), .Q(R3_q), .clr(Reset));
  Multiplexer #(.select(2), .width(8)) multiplexer_1 (
    .in0(R0_q), .in1(R1_q), .in2(R2_q), .in3(R3_q), .out(A), .sel(RA));
  // Probe on A
  Multiplexer #(.select(2), .width(8)) multiplexer_2 (
    .in0(R0_q), .in1(R1_q), .in2(R2_q), .in3(R3_q), .out(B), .sel(RB));
  // Probe on B
endmodule

module BR_vet (
  input  Reset,
  input  Clk,
  input  [7:0] Dados,
  input  [7:0] R0,
  input  WriteReg,
  input  [1:0] RW,
  input  [1:0] RA,
  input  [1:0] RB,
  output [7:0] A,
  output [7:0] B
);

  wire demultiplexer_1_out0, demultiplexer_1_out1, demultiplexer_1_out2, demultiplexer_1_out3;
  wire [7:0] R1_q, R2_q, R3_q;

  LED led_1 (.in(demultiplexer_1_out0));
  Demultiplexer #(.select(2)) demultiplexer_1 (
    .out0(demultiplexer_1_out0), .out1(demultiplexer_1_out1), .out2(demultiplexer_1_out2),
    .out3(demultiplexer_1_out3), .in(WriteReg), .sel(RW));
  Register R1 (.D(Dados), .en(demultiplexer_1_out1), .clk(Clk), .Q(R1_q), .clr(Reset));
  Register R2 (.D(Dados), .en(demultiplexer_1_out2), .clk(Clk), .Q(R2_q), .clr(Reset));
  Register R3 (.D(Dados), .en(demultiplexer_1_out3), .clk(Clk), .Q(R3_q), .clr(Reset));
  Multiplexer #(.select(2), .width(8)) multiplexer_1 (.in0(R0), .in1(R1_q), .in2(R2_q), .in3(R3_q), .out(A), .sel(RA));
  // Probe on A
  Multiplexer #(.select(2), .width(8)) multiplexer_2 (.in0(R0), .in1(R1_q), .in2(R2_q), .in3(R3_q), .out(B), .sel(RB));
  // Probe on B
endmodule

module ULA_vet (
  input  [7:0] A,
  input  [7:0] B,
  input  Funct,
  output [7:0] S
);

  wire adder_1_cout, subtractor_1_bout;
  wire [7:0] adder_1_out, subtractor_1_out;

  Adder adder_1 (.a(A), .b(B), .out(adder_1_out), .cin(1'b0), .cout(adder_1_cout));
  LED led_1 (.in(adder_1_cout));
  Subtractor subtractor_1 (.a(A), .b(B), .out(subtractor_1_out), .bin(1'b0), .bout(subtractor_1_bout));
  LED led_2 (.in(subtractor_1_bout));
  Multiplexer #(.width(8)) multiplexer_1 (.in0(adder_1_out), .in1(subtractor_1_out), .out(S), .sel(Funct));

  // Notes on the sheet:
  //   A + B
  //   A - B
endmodule

module ULA_seq (
  input  [7:0] A,
  input  [7:0] B,
  input  [1:0] Funct,
  output [7:0] S
);

  wire adder_1_cout, subtractor_1_bout;
  wire [7:0] D0, D1, D2;

  Adder adder_1 (.a(A), .b(B), .out(D0), .cin(1'b0), .cout(adder_1_cout));
  LED led_1 (.in(adder_1_cout));
  Subtractor subtractor_1 (.a(A), .b(B), .out(D1), .bin(1'b0), .bout(subtractor_1_bout));
  LED led_2 (.in(subtractor_1_bout));
  assign D2 = A & B;  // AND_Gate and_1, 8 bits wide
  Multiplexer #(.select(2), .width(8)) multiplexer_1 (
    .in0(D0), .in1(D1), .in2(D1), .in3({8{1'b0}}), .out(S), .sel(Funct));

  // Notes on the sheet:
  //   A + B
  //   A - B
endmodule

module Decodificador (
  input  [3:0] A,
  output [7:0] B
);
endmodule
